# Fritzing sketch ir (saved by Fritzing 0.9.3b)
circuit board: 7.14973cm x 3.64522cm
breadboards: 1

parts:
  BC547 = NPN-Transistor [package="TO92 [THT]"]
  U1 = ESP8266 NodeMCU LoLin module
  LED = LEDs [package=led10mm]
  V1 = DC Power [voltage=6V]

nets:
  N1: BC547.E, U1.GND, V1.V-
  N2: BC547.B, U1.D2
  N3: BC547.C, LED.C
  N4: U1.3V3, LED.A
  N5: U1.Vin, V1.V+

notes:
  Módulo Infravermelho
  Projeto I.A.R.A.
  Gabriel Melém

custom parts:
  ESP8266 NodeMCU LoLin module: ESP8266 based NodeMCU
