# Fritzing sketch irreceiver (saved by Fritzing 0.9.3b)
breadboards: 1

parts:
  U2 = ESP8266 NodeMCU LoLin module
  IR1 = tl1838 [package=THT]

nets:
  N1: U2.D4, IR1.OUT
  3V3: U2.3V3, IR1.VCC
  GND: U2.GND, IR1.GND

custom parts:
  ESP8266 NodeMCU LoLin module: ESP8266 based NodeMCU
  tl1838: The TL1838 is a miniaturized receiver for infrared remote control systems. A PIN diode and a preamplifier are assembled on a lead frame, the epoxy package acts as an IR filter. The demodulated output signal can be directly decoded by a microprocessor.
