# Fritzing sketch pc (saved by Fritzing 0.9.3b)
circuit board: 2.60692cm x 2.89209cm
breadboards: 1

parts:
  U2 = Sharp PC817 [package=THT]
  U1 = ESP8266 ESP01 [part_number=ESP8266 package=THT]
  R1 = Resistor [tolerance=±5% resistance=47 package=THT]
  J2 = female pin header, 2 pins [form="♀ (female)"]
  J1 = male pin header, 2 pins [form="♂ (male)"]
  J3 = Terminal Block - 2 pins [package=THT]
  J4 = female pin header, 3 pins [form="♀ (female)"]

nets:
  N1: U2.Pin_1, R1.Pin_1
  GND: U2.Pin_2, U1.GND, J3.Line_2, J4.pin3
  N2: U2.Pin_4, J2.pin1, J1.pin1
  N3: U2.Pin_3, J2.pin2, J1.pin2
  3.3V: U1.VCC, J4.pin2
  N4: U1.GPIO02, R1.Pin_0
  5V: J3.Line_1, J4.pin1

notes:
  Módulo PC - Projeto I.A.R.A.
  Gabriel Melém

custom parts:
  ESP8266 ESP01: Generic WiFi Module based on the ESP8266 with onboard PCB antenna and UART communications
  Terminal Block - 2 pins: Generic Screw Terminal 8mm
