# Fritzing sketch rele - v3 (saved by Fritzing 0.9.3b)
circuit board: 3.7957cm x 6.61447cm
breadboards: 1

parts:
  R1 = Resistor [tolerance=±5% resistance=4.7k package=THT]
  Q1 = NPN-Transistor [package="TO92 [THT]"]
  D1 = Rectifier Diode [part_number=1N4001 package="300 mil [THT]"]
  J2 = Terminal Block - 3 pins [package=THT]
  RLY2 = Relay [part_number=JQC-3F package=THT]
  R2 = Resistor [tolerance=±5% resistance=4.7k package=THT]
  Q2 = NPN-Transistor [package="TO92 [THT]"]
  D2 = Rectifier Diode [part_number=1N4001 package="300 mil [THT]"]
  U1 = ESP8266 ESP01 [part_number=ESP8266 package=THT]
  J1 = Terminal Block - 2 pins [package=THT]
  J3 = Terminal Block - 2 pins [package=THT]
  RLY1 = Relay [part_number=JQC-3F package=THT]
  C1 = Electrolytic Capacitor [capacitance=10µF package="100 mil [THT, electrolytic]"]
  C2 = Electrolytic Capacitor [capacitance=22µF package="100 mil [THT, electrolytic]"]
  D3 = Rectifier Diode [part_number=1N4001 package="300 mil [THT]"]
  R3 = Resistor [tolerance=±5% resistance=120 package=THT]
  R4 = Resistor [tolerance=±5% resistance=200 package=THT]
  U2 = Voltage Regulator - Variable [package="TO220 [THT]"]

nets:
  N1: R1.Pin_0, U1.GPIO02
  N2: R1.Pin_1, Q1.B
  GND: Q1.E, Q2.E, U1.GND, J3.Line_2, C1.-, C2.-, R4.Pin_0
  N3: Q1.C, D1.anode, RLY1.DC_I/O#1
  5V: D1.cathode, RLY2.DC_I/O#2, D2.cathode, J3.Line_1, RLY1.DC_I/O#2, D3.cathode, U2.IN
  N4: J2.Line_1, RLY2.Line, RLY1.Line
  N5: J2.Line_2, RLY2.OFF
  N6: J2.Line_3, RLY2.ON
  N7: RLY2.DC_I/O#1, Q2.C, D2.anode
  N8: R2.Pin_0, U1.GPIO00
  N9: R2.Pin_1, Q2.B
  3.3V: U1.VCC, C2.+, D3.anode, R3.Pin_1, U2.OUT
  N10: J1.Line_1, RLY1.OFF
  N11: J1.Line_2, RLY1.ON
  N12: C1.+, R3.Pin_0, R4.Pin_1, U2.ADJ

notes:
  Módulo Relé V3 - Gabriel Melém

custom parts:
  Terminal Block - 3 pins: Generic Screw Terminal 8mm
  Relay: An SPDT relay.
  ESP8266 ESP01: Generic WiFi Module based on the ESP8266 with onboard PCB antenna and UART communications
  Terminal Block - 2 pins: Generic Screw Terminal 8mm
