# Fritzing sketch rele - v2 (saved by Fritzing 0.9.3b)
circuit board: 3.82132cm x 6.09465cm
breadboards: 1

parts:
  R1 = Resistor [tolerance=±5% resistance=4.7k package=THT]
  Q1 = NPN-Transistor [package="TO92 [THT]"]
  D1 = Rectifier Diode [part_number=1N4001 package="300 mil [THT]"]
  J2 = Terminal Block - 3 pins [package=THT]
  RLY2 = Relay [part_number=JQC-3F package=THT]
  R2 = Resistor [tolerance=±5% resistance=4.7k package=THT]
  Q2 = NPN-Transistor [package="TO92 [THT]"]
  D2 = Rectifier Diode [part_number=1N4001 package="300 mil [THT]"]
  U1 = ESP8266 ESP01 [part_number=ESP8266 package=THT]
  J1 = Terminal Block - 2 pins [package=THT]
  J3 = Terminal Block - 2 pins [package=THT]
  J4 = female pin header, 3 pins [form="♀ (female)"]
  RLY1 = Relay [part_number=JQC-3F package=THT]

nets:
  N1: R1.Pin_0, U1.GPIO02
  N2: R1.Pin_1, Q1.B
  GND: Q1.E, Q2.E, U1.GND, J3.Line_2, J4.pin3
  N3: Q1.C, D1.anode, RLY1.DC_I/O#1
  5V: D1.cathode, RLY2.DC_I/O#2, D2.cathode, J3.Line_1, J4.pin1, RLY1.DC_I/O#2
  N4: J2.Line_1, RLY2.Line, RLY1.Line
  N5: J2.Line_2, RLY2.OFF
  N6: J2.Line_3, RLY2.ON
  N7: RLY2.DC_I/O#1, Q2.C, D2.anode
  N8: R2.Pin_0, U1.GPIO00
  N9: R2.Pin_1, Q2.B
  3.3V: U1.VCC, J4.pin2
  N10: J1.Line_1, RLY1.OFF
  N11: J1.Line_2, RLY1.ON

notes:
  Módulo Relé V2
  Gabriel Melém

custom parts:
  Terminal Block - 3 pins: Generic Screw Terminal 8mm
  Relay: An SPDT relay.
  ESP8266 ESP01: Generic WiFi Module based on the ESP8266 with onboard PCB antenna and UART communications
  Terminal Block - 2 pins: Generic Screw Terminal 8mm
