# Fritzing sketch rele_r3 (saved by Fritzing 0.9.3b)
circuit board: 4.20471cm x 9.76956cm
breadboards: 1

parts:
  U1 = ESP8266 NodeMCU LoLin module
  J1 = Terminal Block - 3 pins [package=THT]
  RLY1 = Relay [part_number=JQC-3F package=THT]
  R1 = Resistor [tolerance=±5% resistance=4.7k package=THT]
  Q1 = NPN-Transistor [package="TO92 [THT]"]
  D1 = Rectifier Diode [part_number=1N4001 package="300 mil [THT]"]
  J2 = Terminal Block - 3 pins [package=THT]
  RLY2 = Relay [part_number=JQC-3F package=THT]
  R2 = Resistor [tolerance=±5% resistance=4.7k package=THT]
  Q2 = NPN-Transistor [package="TO92 [THT]"]
  D2 = Rectifier Diode [part_number=1N4001 package="300 mil [THT]"]

nets:
  GND: U1.GND, Q1.E, Q2.E
  N1: U1.D5, R1.Pin_0
  N2: U1.D6, R2.Pin_0
  5V: U1.VU, RLY1.DC_I/O#2, D1.cathode, RLY2.DC_I/O#2, D2.cathode
  N3: J1.Line_1, RLY1.Line, J2.Line_1, RLY2.Line
  N4: J1.Line_2, RLY1.OFF
  N5: J1.Line_3, RLY1.ON
  N6: RLY1.DC_I/O#1, Q1.C, D1.anode
  N7: R1.Pin_1, Q1.B
  N8: J2.Line_2, RLY2.OFF
  N9: J2.Line_3, RLY2.ON
  N10: RLY2.DC_I/O#1, Q2.C, D2.anode
  N11: R2.Pin_1, Q2.B

notes:
  Gabriel Melém
  Módulo Relé - Rev.3
  Projeto I.A.R.A.

custom parts:
  ESP8266 NodeMCU LoLin module: ESP8266 based NodeMCU
  Terminal Block - 3 pins: Generic Screw Terminal 8mm
  Relay: An SPDT relay.
